// Logisim project Processador8bits.circ as structural Verilog: 6 circuits, main circuit Banco de registradores
module Banco_de_registradores (
  input  [7:0] Dado_a_ser_escrito,
  input  escrever_reg,
  input  [1:0] \endereço_do_Reg_1 ,
  input  [1:0] \endereço_do_Reg_2 ,
  input  Clear,
  input  Clock,
  output [7:0] REG_00,
  output [7:0] REG_01,
  output [7:0] REG_10,
  output [7:0] REG_11,
  output [7:0] saida_do_reg_1,
  output [7:0] saida_do_reg_2
);

  wire demultiplexer_1_out0, demultiplexer_1_out1, demultiplexer_1_out2, demultiplexer_1_out3;

  Demultiplexer #(.select(2), .enable("false")) demultiplexer_1 (
    .out0(demultiplexer_1_out0), .out1(demultiplexer_1_out1), .out2(demultiplexer_1_out2),
    .out3(demultiplexer_1_out3), .in(escrever_reg), .sel(\endereço_do_Reg_1 ));
  Register register_1 (.D(Dado_a_ser_escrito), .en(demultiplexer_1_out0), .Q(REG_00), .clk(Clock), .clr(Clear));
  Register register_2 (.D(Dado_a_ser_escrito), .en(demultiplexer_1_out1), .Q(REG_01), .clk(Clock), .clr(Clear));
  Register register_3 (.D(Dado_a_ser_escrito), .en(demultiplexer_1_out2), .Q(REG_10), .clk(Clock), .clr(Clear));
  Register register_4 (.D(Dado_a_ser_escrito), .en(demultiplexer_1_out3), .Q(REG_11), .clk(Clock), .clr(Clear));
  Multiplexer #(.select(2), .width(8), .enable("false")) multiplexer_1 (
    .in0(REG_00), .in1(REG_01), .in2(REG_10), .in3(REG_11), .out(saida_do_reg_1), .sel(\endereço_do_Reg_1 ));
  Multiplexer #(.select(2), .width(8), .enable("false")) multiplexer_2 (
    .in0(REG_00), .in1(REG_01), .in2(REG_10), .in3(REG_11), .out(saida_do_reg_2), .sel(\endereço_do_Reg_2 ));
endmodule

module Unidade_de_controle (
  input  [2:0] OPtipo,
  input  [2:0] OPcode,
  output \Endereço ,
  output Jump,
  output Branch,
  output [1:0] MemtoReg,
  output [2:0] ALUOP,
  output Formato____R,
  output MemWrite_MemRead,
  output Formato___I,
  output ALUSrc,
  output Formato___J,
  output RegWrite
);

  Multiplexer #(.select(3), .width(3)) multiplexer_1 (
    .in0(3'b010), .in1(3'b001), .in2(3'b001), .in3(3'b001), .in4(3'b010), .in5(3'b010), .in6(3'b010),
    .in7(3'b100), .out({Formato___J, Formato___I, Formato____R}), .sel(OPtipo));  // open: en
  Multiplexer #(.select(3), .width(11)) multiplexer_2 (
    .in0(11'h408), .in1(11'h4a8), .in2(11'h4c8), .in3(11'h4e8), .in4(11'h411), .in5(11'h101), .in6(11'hc4),
    .in7(11'h2), .out({RegWrite, ALUSrc, MemWrite_MemRead, ALUOP, MemtoReg, Branch, Jump, \Endereço }),
    .sel(OPcode));  // open: en

  // Notes on the sheet:
  //   SW - 101
  //   BEQ - 110
  //   JUMP - 111
  //   MOVE - 000 
  //   ADD - 001 
  //   SUB - 010
  //   MULT - 011
  //   LW - 100
endmodule

module \Memória_de_dados  (
  input  [7:0] dado_a_ser_escrito,
  input  [7:0] seletor,
  input  Enable_do_seletor,
  input  clock,
  input  load,
  input  clear,
  output [7:0] dado_lido
);

  wire not_1_out;

  assign dado_lido = not_1_out ? dado_a_ser_escrito : 8'bz;  // Controlled_Buffer controlled_buffer_1
  not not_1 (not_1_out, load);
  RAM ram_1 (.addr(seletor), .data(dado_lido), .sel(Enable_do_seletor), .clk(clock), .ld(load), .clr(clear));
endmodule

module ALU (
  input  [2:0] \Endereço ,
  input  [7:0] in_2,
  input  [7:0] in_3,
  output [7:0] Saida,
  output Zero,
  output Overflow
);

  wire adder_1_cout, subtractor_1_bout;
  wire [7:0] adder_1_out, and_1_out, multiplier_1_out, not_1_out, not_2_out, not_3_out, or_1_out,
       subtractor_1_out;

  assign not_1_out = ~and_1_out;  // NOT_Gate not_1, 8 bits wide
  assign and_1_out = in_2 & in_3;  // AND_Gate and_1, 8 bits wide
  assign or_1_out = in_2 | in_3;  // OR_Gate or_1, 8 bits wide
  Multiplexer #(.select(3), .width(8)) multiplexer_1 (
    .in0(and_1_out), .in1(not_1_out), .in2(or_1_out), .in3(not_2_out), .in4(not_3_out), .in5(adder_1_out),
    .in6(subtractor_1_out), .in7(multiplier_1_out), .out(Saida), .sel(\Endereço ));  // open: en
  assign not_2_out = ~or_1_out;  // NOT_Gate not_2, 8 bits wide
  assign not_3_out = ~in_2;  // NOT_Gate not_3, 8 bits wide
  Adder adder_1 (.a(in_2), .b(in_3), .out(adder_1_out), .cout(adder_1_cout));  // open: cin
  Subtractor subtractor_1 (.a(in_2), .b(in_3), .out(subtractor_1_out), .bout(subtractor_1_bout));  // open: bin
  Multiplier multiplier_1 (.a(in_2), .b(in_3), .out(multiplier_1_out));  // open: cin, cout
  Comparator comparator_1 (.a(in_2), .b(in_3), .eq(Zero));  // open: gt, lt
  or or_2 (Overflow, subtractor_1_bout, adder_1_cout);
endmodule

module CPU (
  input  Limpar,
  input  Limpar_2,
  input  Limpar_3,
  input  Limpar_4,
  input  in_5,
  input  in_6,
  output [7:0] \Instrução ,
  output [7:0] out_8,
  output [7:0] out_9,
  output [7:0] out_10,
  output [2:0] ULAOp,
  output [7:0] \Endereço ,
  output [7:0] out_13,
  output [7:0] out_14,
  output [7:0] out_15,
  output [7:0] out_16,
  output [7:0] out_17
);

  wire alu_1_zero, and_1_out, and_2_out, CLOCK, \memória_de_instrução_1_p3 , \memória_de_instrução_1_p4 ,
       \memória_de_instrução_1_p5 , not_1_out, not_2_out, not_3_out, unidade_de_controle_1_alusrc,
       unidade_de_controle_1_branch, \unidade_de_controle_1_endereço , unidade_de_controle_1_jump,
       unidade_de_controle_1_memwrite_memread, unidade_de_controle_1_regwrite;
  wire [1:0] \memória_de_instrução_1_p8 , \memória_de_instrução_1_p9 , unidade_de_controle_1_memtoreg;
  wire [2:0] \memória_de_instrução_1_p6 ;
  wire [7:0] banco_de_registradores_1_saida_do_reg_2, \memória_de_dados_1_dado_lido ,
       \memória_de_instrução_1_p7 , multiplexer_1_out, multiplexer_3_out;

  not not_1 (not_1_out, and_1_out);
  Counter counter_1 (
    .load(not_1_out), .D(\memória_de_instrução_1_p7 ), .count(and_1_out), .Q(\Endereço ), .clk(CLOCK),
    .clr(Limpar_3));  // open: carry
  Clock clock_1 (.out(CLOCK));
  RAM ram_1 (.addr(\Endereço ), .data(\Instrução ), .clk(CLOCK), .clr(Limpar));  // open: sel, ld
  // Memória_de_Instrução memória_de_instrução_1: pin names not known; wires that end beside it: \Instrução , Limpar_4, \memória_de_instrução_1_p3 , \memória_de_instrução_1_p4 , \memória_de_instrução_1_p5 , \memória_de_instrução_1_p6 , \memória_de_instrução_1_p7 , \memória_de_instrução_1_p8 , \memória_de_instrução_1_p9 
  Multiplexer #(.select(2), .width(8), .disabled(0), .enable("false")) multiplexer_1 (
    .in0(\memória_de_instrução_1_p7 ), .in1(out_10), .in2(\memória_de_dados_1_dado_lido ),
    .out(multiplexer_1_out), .sel(unidade_de_controle_1_memtoreg));  // open: in3
  and and_1 (and_1_out, not_3_out, not_2_out);
  not not_2 (not_2_out, unidade_de_controle_1_jump);
  Unidade_de_controle unidade_de_controle_1 (
    .OPcode(\Instrução [2:0]), .Jump(unidade_de_controle_1_jump), .Branch(unidade_de_controle_1_branch),
    .ALUOP(ULAOp), .MemWrite_MemRead(unidade_de_controle_1_memwrite_memread),
    .ALUSrc(unidade_de_controle_1_alusrc), .RegWrite(unidade_de_controle_1_regwrite),
    .MemtoReg(unidade_de_controle_1_memtoreg), .\Endereço (\unidade_de_controle_1_endereço ),
    .Formato___I(\memória_de_instrução_1_p4 ), .Formato___J(\memória_de_instrução_1_p5 ),
    .Formato____R(\memória_de_instrução_1_p3 ), .OPtipo(\memória_de_instrução_1_p6 ));
  Banco_de_registradores banco_de_registradores_1 (
    .Dado_a_ser_escrito(multiplexer_1_out), .saida_do_reg_1(out_8),
    .saida_do_reg_2(banco_de_registradores_1_saida_do_reg_2), .Clear(Limpar_2),
    .\endereço_do_Reg_1 (\memória_de_instrução_1_p8 ), .\endereço_do_Reg_2 (\memória_de_instrução_1_p9 ),
    .Clock(CLOCK), .escrever_reg(unidade_de_controle_1_regwrite), .REG_00(out_13), .REG_01(out_14),
    .REG_10(out_15), .REG_11(out_16));
  not not_3 (not_3_out, and_2_out);
  Multiplexer #(.width(8), .disabled(0), .enable("false")) multiplexer_2 (
    .in0(banco_de_registradores_1_saida_do_reg_2), .in1(\memória_de_instrução_1_p7 ), .out(out_9),
    .sel(unidade_de_controle_1_alusrc));
  and and_2 (and_2_out, unidade_de_controle_1_branch, alu_1_zero);
  ALU alu_1 (.Saida(out_10), .\Endereço (ULAOp), .Zero(alu_1_zero), .in_2(out_8), .in_3(out_9));  // open: Overflow
  Multiplexer #(.width(8), .disabled(0), .enable("false")) multiplexer_3 (
    .in0(out_10), .in1(\memória_de_instrução_1_p7 ), .out(multiplexer_3_out),
    .sel(\unidade_de_controle_1_endereço ));
  \Memória_de_dados  \memória_de_dados_1  (
    .dado_lido(\memória_de_dados_1_dado_lido ), .dado_a_ser_escrito(banco_de_registradores_1_saida_do_reg_2),
    .seletor(multiplexer_3_out), .Enable_do_seletor(unidade_de_controle_1_memwrite_memread), .load(in_5),
    .clear(in_6), .clock(CLOCK));

  assign out_17 = out_10;

  // Other names for the same wires on the sheet: a[7:0] = out_8; b[7:0] = out_9; reg_00[7:0] = out_13;
  //   reg_01[7:0] = out_14; reg_10[7:0] = out_15; reg_11[7:0] = out_16; s[7:0] = out_10

  // Notes on the sheet:
  //   Instrução
  //   Tipo - R
  //   Tipo - I
  //   Tipo - J
  //   Tipo - R
  //   Tipo - I
  //   Branch
  //   Tipo - J
  //   MemtoReg
  //   MEM read/write
  //   RegWrite
  //   Jump
  //   ALUOp
  //   ALUSrc
endmodule

module \Memória_de_Instrução  (
  input  Tipo_R,
  input  Tipo_I,
  input  Tipo_J,
  input  [7:0] \Instrução ,
  output [7:0] OP,
  output [7:0] OP_2,
  output [7:0] OP_3,
  output [1:0] Reg1,
  output [7:0] OP_4,
  output [1:0] Reg2,
  output [2:0] Opcode,
  output [7:0] INPUT
);

  Multiplexer #(.select(3), .width(8)) multiplexer_1 (
    .in2({{6{1'b0}}, OP_2[6:5]}), .in4({3'b000, OP_3[7:3]}), .out(INPUT), .sel({Tipo_J, Tipo_I, Tipo_R}));  // open: in0, in1, in3, in5, in6, in7, en
  Demultiplexer #(.select(3), .width(8)) demultiplexer_1 (
    .out1(OP), .out2({OP_2[7:5], OP[4:3], OP_2[2:0]}), .out4(OP_3), .in(\Instrução ),
    .sel({Tipo_J, Tipo_I, Tipo_R}));  // open: out0, out3, out5, out6, out7, en

  assign OP_2[4:3] = OP[4:3];
  assign OP_4 = \Instrução ;
  assign Opcode = \Instrução [2:0];
  assign Reg1 = OP[4:3];
  assign Reg2 = OP[6:5];
  // also tied to GND on the sheet: {OP[7], OP_2[7]}

  // Notes on the sheet:
  //   bit vago
  //   bit vago
  //   Tipo - I
  //   Tipo - J
  //   Tipo - R
endmodule
